// Logisim project Task_5.circ as structural Verilog: 1 circuit, main circuit main
module main (
  output Y1,
  output Y2
);

  wire and_1_out, button_1_out, clock_1_out, T1_qn, T2_q;

  Button button_1 (.out(button_1_out));
  Clock clock_1 (.out(clock_1_out));
  T_Flip_Flop T1 (.T(button_1_out), .clk(clock_1_out), .Q(Y1), .Qn(T1_qn));  // open: reset, preset
  T_Flip_Flop T2 (.T(and_1_out), .clk(clock_1_out), .Q(T2_q));  // open: Qn, reset, preset
  and and_1 (and_1_out, T1_qn, button_1_out);
  and and_2 (Y2, T1_qn, T2_q);
endmodule
